# Fritzing sketch Buttons_with_GPIO_2 (saved by Fritzing 0.9.1b)
breadboards: 2

parts:
  Lid_Conn1 = RaspberrySTEM Lid Connector
  S1 = Pushbutton [package="[THT]"]

nets:
  N1: Lid_Conn1.pin8, S1.Pin_1, S1.Pin_2
  N2: Lid_Conn1.pin_39, S1.Pin_3, S1.Pin_4

notes:
  top-left
  top-right
  bottom-left
  bot
