# Fritzing sketch LED_Matrix (saved by Fritzing 0.9.1b)
breadboards: 2

parts:
  Lid_Conn1 = RaspberrySTEM Lid Connector
  IC2 = LED MAtrix [chip_label=IC]

nets:
  N1: Lid_Conn1.pin_19, IC2.pin3
  N2: Lid_Conn1.pin_21, IC2.pin_9
  N3: Lid_Conn1.pin_23, Lid_Conn1.pin_39, IC2.pin1, IC2.pin2, IC2.pin5, IC2.pin6
  N4: Lid_Conn1.pin_24, IC2.pin4
  N5: IC2.pin7, IC2.pin8
  N6: IC2.pin_11, IC2.pin_12

notes:
  top-left
  top-right
  bottom-left
  bot
  RST is left unconnected
