# Fritzing sketch LED_Matrix_Accel_Buttons (saved by Fritzing 0.9.1b)
breadboards: 2

parts:
  Lid_Conn1 = RaspberrySTEM Lid Connector
  IC2 = LED MAtrix [chip_label=IC]
  IC3 = Accelerometer [chip_label=?]
  S1 = Pushbutton [package="[THT]"]

nets:
  N1: Lid_Conn1.pin1, IC3.pin1
  N2: Lid_Conn1.pin3, IC3.pin3
  N3: Lid_Conn1.pin5, IC3.pin2
  N4: Lid_Conn1.pin_19, IC2.pin3
  N5: Lid_Conn1.pin_21, IC2.pin_9
  N6: Lid_Conn1.pin_23, Lid_Conn1.pin_39, IC2.pin1, IC2.pin2, IC2.pin5, IC2.pin6, IC3.pin4, S1.Pin_3, S1.Pin_4
  N7: Lid_Conn1.pin_24, IC2.pin4
  N8: Lid_Conn1.pin_26, S1.Pin_1, S1.Pin_2
  N9: IC2.pin7, IC2.pin8
  N10: IC2.pin_11, IC2.pin_12

notes:
  top-left
  top-right
  bottom-left
  bot
  RST is left unconnected
