# Fritzing sketch LED_Matrix_Fully_Connected (saved by Fritzing 0.9.1b)
breadboards: 1

parts:
  Lid_Conn1 = RaspberrySTEM Lid Connector
  IC1 = DIP - 8 pins [chip_label=IC package="DIP (Dual Inline) [THT]"]

nets:
  N1: Lid_Conn1.pin1, Lid_Conn1.pin_23, IC1.pin1, IC1.pin2
  N2: Lid_Conn1.pin_19, IC1.pin_9
  N3: Lid_Conn1.pin_21, IC1.pin3
  N4: Lid_Conn1.pin_24, IC1.pin4
  N5: Lid_Conn1.pin_39, IC1.pin5, IC1.pin6
  N6: IC1.pin7, IC1.pin8
  N7: IC1.pin_11, IC1.pin_12

notes:
  RST is left unconnected

custom parts:
  DIP - 8 pins: A DIP stand-in part for whatever IC you want. With 8 pins on a 300mil dual inline package (DIP) footprint.
