# Fritzing sketch LED_Matrix_unconnected (saved by Fritzing 0.9.1b)
breadboards: 2

parts:
  Lid_Conn1 = RaspberrySTEM Lid Connector  # not connected
  IC3 = LED MAtrix [chip_label=IC]

nets:
  N1: IC3.pin1, IC3.pin2
  N2: IC3.pin5, IC3.pin6
  N3: IC3.pin7, IC3.pin8
  N4: IC3.pin_11, IC3.pin_12

notes:
  top-left
  top-right
  bottom-left
  bot
