# Fritzing sketch Many_Buttons (saved by Fritzing 0.9.1b)
breadboards: 2

parts:
  Lid_Conn1 = RaspberrySTEM Lid Connector
  S1 = Pushbutton [package="[THT]"]
  S2 = Pushbutton [package="[THT]"]
  S3 = Pushbutton [package="[THT]"]
  S4 = Pushbutton [package="[THT]"]

nets:
  N1: Lid_Conn1.pin8, S1.Pin_3, S1.Pin_4
  N2: Lid_Conn1.pin_10, S4.Pin_3, S4.Pin_4
  N3: Lid_Conn1.pin_22, S3.Pin_1, S3.Pin_2
  N4: Lid_Conn1.pin_26, S2.Pin_1, S2.Pin_2
  N5: Lid_Conn1.pin_39, S1.Pin_1, S1.Pin_2, S2.Pin_3, S2.Pin_4, S3.Pin_3, S3.Pin_4, S4.Pin_1, S4.Pin_2

notes:
  top-left
  top-right
  bottom-left
  bot
