# Fritzing sketch Minecraft_1button (saved by Fritzing 0.9.1b)
breadboards: 2

parts:
  Lid_Conn1 = RaspberrySTEM Lid Connector
  S2 = Pushbutton [package="[THT]"]

nets:
  N1: Lid_Conn1.pin_18, S2.Pin_3, S2.Pin_4
  N2: Lid_Conn1.pin_39, S2.Pin_1, S2.Pin_2

notes:
  top-left
  top-right
  bottom-left
  bot
