# Fritzing sketch Minecraft_Matrix_Accel_4way_2buttons (saved by Fritzing 0.9.1b)
breadboards: 2

parts:
  Lid_Conn1 = RaspberrySTEM Lid Connector
  IC2 = LED MAtrix [chip_label=IC]
  IC3 = Accelerometer [chip_label=?]
  S1 = Pushbutton [package="[THT]"]
  S2 = Pushbutton [package="[THT]"]
  S3 = Pushbutton [package="[THT]"]
  S4 = Pushbutton [package="[THT]"]
  S5 = Pushbutton [package="[THT]"]
  S6 = Pushbutton [package="[THT]"]

nets:
  N1: Lid_Conn1.pin1, Lid_Conn1.pin_23, IC2.pin1, IC2.pin2, IC3.pin1
  N2: Lid_Conn1.pin3, IC3.pin3
  N3: Lid_Conn1.pin5, IC3.pin2
  N4: Lid_Conn1.pin8, Lid_Conn1.pin_10
  N5: Lid_Conn1.pin_12, S5.Pin_1, S5.Pin_2
  N6: Lid_Conn1.pin_16, S4.Pin_3, S4.Pin_4
  N7: Lid_Conn1.pin_18, S3.Pin_1, S3.Pin_2
  N8: Lid_Conn1.pin_19, IC2.pin3
  N9: Lid_Conn1.pin_21, IC2.pin_9
  N10: Lid_Conn1.pin_24, IC2.pin4
  N11: Lid_Conn1.pin_26, S1.Pin_1, S1.Pin_2
  N12: Lid_Conn1.pin_39, IC2.pin5, IC2.pin6, IC3.pin4, S1.Pin_3, S1.Pin_4, S2.Pin_1, S2.Pin_2, S3.Pin_3, S3.Pin_4, S4.Pin_1, S4.Pin_2, S5.Pin_3, S5.Pin_4, S6.Pin_1, S6.Pin_2
  N13: IC2.pin7, IC2.pin8
  N14: IC2.pin_11, IC2.pin_12
  N15: S2.Pin_3, S2.Pin_4
  N16: S6.Pin_3, S6.Pin_4

notes:
  top-left
  top-right
  bottom-left
  bot
