# Fritzing sketch Your_First_Breadboard (saved by Fritzing 0.9.1b)
breadboards: 2

parts:
  CELL1 = Coin Cell  # not connected
  R1 = Resistor [tolerance=±5% resistance=220 package=THT]
  R2 = Resistor [tolerance=±5% resistance=220 package=THT]
  LED1 = LED - 5mm [color="Red (633nm)" package="5 mm [THT]"]

nets:
  N1: R1.Pin_1, LED1.cathode
  N2: R2.Pin_0, LED1.anode

notes:
  top-left
  top-right
  bottom-left
  bot

custom parts:
  Coin Cell: CR2025 Coin Cell
