# Fritzing sketch Your_First_Breadboard_Remove_Battery (saved by Fritzing 0.9.1b)
breadboards: 2

parts:
  R2 = Resistor [tolerance=±5% resistance=220 package=THT]
  LED1 = LED - 5mm [color="Red (633nm)" package="5 mm [THT]"]
  Lid_Conn1 = RaspberrySTEM Lid Connector  # not connected

nets:
  N1: R2.Pin_0, LED1.anode

notes:
  top-left
  top-right
  bottom-left
  bot
