# Fritzing sketch breadboard-2 (saved by Fritzing 0.9.1b)
breadboards: 1

parts:
  Battery = Battery
  Resistor = Resistor [tolerance=±5% resistance=220 package=THT]

nets:
  N1: Battery.+, Resistor.Pin_1
