# Fritzing sketch first_circuit-6 (saved by Fritzing 0.9.1b)

parts:
  Battery = Battery
  LED = LED - 5mm [color="Red (633nm)" package="5 mm [THT]"]
  Resistor = Resistor [tolerance=±5% resistance=220 package=THT]

nets:
  N1: Battery.-, LED.cathode
  N2: Battery.+, Resistor.Pin_0
  N3: LED.anode, Resistor.Pin_1
