# Fritzing sketch first_circuit_on_breadboard-2 (saved by Fritzing 0.9.1b)
breadboards: 1

parts:
  LED = LED - 5mm [color="Red (633nm)" package="5 mm [THT]"]
  Resistor = Resistor [tolerance=±5% resistance=220 package=THT]
  Lid_Conn1 = RaspberrySTEM Lid Connector

nets:
  N1: LED.cathode, Lid_Conn1.pin_39
  N2: LED.anode, Resistor.Pin_0
  N3: Resistor.Pin_1, Lid_Conn1.pin1
