# Fritzing sketch first_circuit_on_breadboard-schem (saved by Fritzing 0.9.1b)
breadboards: 1

parts:
  LED = LED - 5mm [color="Red (633nm)" package="5 mm [THT]"]
  Resistor = Resistor [tolerance=±5% resistance=220 package=THT]

nets:
  GND: LED.cathode
  N1: LED.anode, Resistor.Pin_0
  3.3V: Resistor.Pin_1
