# Fritzing sketch gpio-schem-2 (saved by Fritzing 0.9.1b)
breadboards: 1

parts:
  LED = LED - 5mm [color="Red (633nm)" package="5 mm [THT]"]
  Resistor = Resistor [tolerance=±5% resistance=220 package=THT]

nets:
  3.3V: LED.cathode, Resistor.Pin_1
  N1: LED.anode, Resistor.Pin_0
