# Fritzing sketch simon-4but-4led (saved by Fritzing 0.9.1b)
breadboards: 2

parts:
  Lid_Conn1 = RaspberrySTEM Lid Connector
  S1 = Pushbutton [package="[THT]"]
  S2 = Pushbutton [package="[THT]"]
  S3 = Pushbutton [package="[THT]"]
  S4 = Pushbutton [package="[THT]"]
  S5 = Pushbutton [package="[THT]"]
  S6 = Pushbutton [package="[THT]"]
  LED1 = LED - 5mm [color="Red (635nm)" package="5 mm [THT]"]
  LED2 = LED - 5mm [color="Orange (620nm)" package="5 mm [THT]"]
  LED3 = LED - 5mm [color="Yellow (595nm)" package="5 mm [THT]"]
  LED4 = LED - 5mm [color="Green (560nm)" package="5 mm [THT]"]
  R1 = Resistor [tolerance=±5% resistance=220 package=THT]
  R2 = Resistor [tolerance=±5% resistance=220 package=THT]
  R3 = Resistor [tolerance=±5% resistance=220 package=THT]
  R4 = Resistor [tolerance=±5% resistance=220 package=THT]

nets:
  N1: Lid_Conn1.pin7, LED2.cathode
  N2: Lid_Conn1.pin8, S1.Pin_1, S1.Pin_2
  N3: Lid_Conn1.pin_10, Lid_Conn1.pin_11, S2.Pin_1, S2.Pin_2, S2.Pin_3, S2.Pin_4, S3.Pin_1, S3.Pin_2, S3.Pin_3, S3.Pin_4
  N4: Lid_Conn1.pin_12, LED3.cathode
  N5: Lid_Conn1.pin_13, LED4.cathode
  N6: Lid_Conn1.pin_16, S4.Pin_3, S4.Pin_4
  N7: Lid_Conn1.pin_17, R1.Pin_1, R2.Pin_0, R3.Pin_0, R4.Pin_1
  N8: Lid_Conn1.pin_18, LED1.cathode
  N9: Lid_Conn1.pin_39, S1.Pin_3, S1.Pin_4, S4.Pin_1, S4.Pin_2, S5.Pin_1, S5.Pin_2, S5.Pin_3, S5.Pin_4, S6.Pin_1, S6.Pin_2, S6.Pin_3, S6.Pin_4
  N10: LED1.anode, R4.Pin_0
  N11: LED2.anode, R1.Pin_0
  N12: LED3.anode, R2.Pin_1
  N13: LED4.anode, R3.Pin_1

notes:
  top-left
  top-right
  bottom-left
  bot
